# Fritzing sketch glyph_game (saved by Fritzing 0.9.2b)
breadboards: 1

parts:
  Part1 = RFID-RC522
  Part2 = RFID-RC522
  Part3 = RFID-RC522
  Part4 = RFID-RC522
  Part5 = Arduino Pro Mini v13
  LED1 = RGB LED - (4 legs) [package="5 mm [THT]"]
  LED2 = RGB LED - (4 legs) [package="5 mm [THT]"]
  LED3 = RGB LED - (4 legs) [package="5 mm [THT]"]
  LED4 = RGB LED - (4 legs) [package="5 mm [THT]"]
  R1 = Resistor [tolerance=±5% resistance=400 package=THT]
  R2 = Resistor [tolerance=±5% resistance=170 package=THT]
  R3 = Resistor [tolerance=±5% resistance=2.8k package=THT]
  Part6 = Arduino Uno (Rev3)  # not connected

nets:
  N1: Part1.MOSI, Part2.MOSI, Part3.MOSI
  N2: Part2.SDA, Part3.SDA
  N3: Part2.SCK, Part3.SCK
  N4: Part2.MISO, Part3.MISO
  GND: Part3.GND, Part4.GND, Part5.GND, LED1.green_cathode, LED2.green_cathode, LED3.green_cathode, LED4.green_cathode, R3.Pin_1
  N5: Part3.3_3V, Part4.3_3V, R2.Pin_1, R3.Pin_0
  N6: Part4.RST, Part5.D8
  N7: Part5.VCC, LED1.common_anode, LED2.common_anode, LED3.common_anode, LED4.common_anode, R2.Pin_0
  N8: Part5.D9_PWM, R1.Pin_0
  N9: LED1.red_cathode, R1.Pin_1
  N10: LED1.blue_cathode, LED2.red_cathode
  N11: LED2.blue_cathode, LED3.red_cathode
  N12: LED3.blue_cathode, LED4.red_cathode

custom parts:
  RFID-RC522: The simple China made RFID reader
